# Fritzing sketch teensy-4.0.fzpz(4) (saved by Fritzing 1.0.2b)
breadboards: 1

parts:
  Tri-Colour_LED = RGB LED (com. cathode, rgb) [package="5 mm [THT]"]
  Resistor_(Green) = Resistor [tolerance=±5% resistance=220 package="2512 [SMD]"]
  Resistor_(Blue) = Resistor [tolerance=±5% resistance=220 package="2512 [SMD]"]
  Resistor_(Red) = Resistor [tolerance=±5% resistance=220 package="2512 [SMD]"]
  Teensy_3_2 = Teensy 3.2  # not connected
  S2 = Pushbutton [package="[THT]"]
  S3 = Pushbutton [package="[THT]"]
  Resistor_(Red)1 = Resistor [tolerance=±5% resistance=10K package="2512 [SMD]"]

nets:
  N1: Tri-Colour_LED.red_anode, Resistor_(Green).Pin_0
  N2: Tri-Colour_LED.common_cathode, S2.Pin_1, S2.Pin_2, S2.Pin_3, S2.Pin_4, S3.Pin_1, S3.Pin_2, S3.Pin_3, S3.Pin_4, Resistor_(Red)1.Pin_0
  N3: Tri-Colour_LED.green_anode, Resistor_(Blue).Pin_0
  N4: Tri-Colour_LED.blue_anode, Resistor_(Red).Pin_0

notes:
  CST8227 – Interfacing
  Lab 04 – Pushbuttons to Control LED Colors
  Control a tri-color RGB with two switches and a pull-up resistor.
  @ author Sahil Kakadiya (kaka0030)

custom parts:
  Teensy 3.2: The Teensy is a complete USB-based microcontoller development system, in a very small footprint, capable of implementing many types of projects. All programming is done via the USB port. No special programmer is needed, only a standard micro-USB cable and a PC or Macintosh with a USB port. It has a USB keyboard/mouse/joystick emulation stack and can be programmed through Arduino IDE.
