# Fritzing sketch teensy-4.0.fzpz(5) (saved by Fritzing 1.0.2b)
breadboards: 1

parts:
  Tri-Colour_LED = RGB LED (com. cathode, rgb) [package="5 mm [THT]"]
  Resistor_(Green) = Resistor [tolerance=±5% resistance=220 package="2512 [SMD]"]
  Resistor_(Blue) = Resistor [tolerance=±5% resistance=220 package="2512 [SMD]"]
  Resistor_(Red) = Resistor [tolerance=±5% resistance=220 package="2512 [SMD]"]
  Teensy_3_2 = Teensy 3.2  # not connected
  all = Resistor [tolerance=±5% resistance=10K package="2512 [SMD]"]
  R1 = 6mm Trimmer Potentiometer [maximum_resistance=10kΩ knob_status=50% power=0.5W package=THT]
  R2 = Temperature Sensor (Thermistor) [thermistor_type=NTC package=THT]

nets:
  N1: Tri-Colour_LED.red_anode, Resistor_(Green).Pin_0
  N2: Tri-Colour_LED.common_cathode, all.Pin_1, R1.leg2
  N3: Tri-Colour_LED.green_anode, Resistor_(Blue).Pin_0
  N4: Tri-Colour_LED.blue_anode, Resistor_(Red).Pin_0
  N5: all.Pin_0, R2.pin_1
  N6: R1.leg1, R2.pin_0

notes:
  CST8227 – Interfacing
  Lab 06 – Analog Input
  Control a tri-color RGB with two switches and a pull-up resistor.
  @ author Sahil Kakadiya (kaka0030)

custom parts:
  Teensy 3.2: The Teensy is a complete USB-based microcontoller development system, in a very small footprint, capable of implementing many types of projects. All programming is done via the USB port. No special programmer is needed, only a standard micro-USB cable and a PC or Macintosh with a USB port. It has a USB keyboard/mouse/joystick emulation stack and can be programmed through Arduino IDE.
